// Logisim project ALU.circ as structural Verilog: 1 circuit, main circuit ALU
module ALU (
  input  in_1,
  input  in_2,
  input  [31:0] A,
  input  [31:0] B,
  input  [4:0] Shift,
  input  CarryIn,
  input  [3:0] Codop,
  output [3:0] Flags,
  output [31:0] S
);

  wire adder_3_cout, ASR, CMN, CMP, LSL, not_1_out, OutAdd, OutSub, ResV, ResVAplusB, ResVsub,
       subtractor_1_bout, subtractor_3_bout, xnor_1_out, xnor_2_out, xor_2_out, xor_3_out, xor_4_out,
       xor_5_out;
  wire [4:0] subtractor_4_out, subtractor_5_out;
  wire [31:0] adder_1_out, adder_3_out, AetB, and_1_out, and_3_out, AplusB, BmoinsA, multiplexer_3_out,
       multiplier_1_out, not_3_out, not_4_out, not_6_out, or_1_out, shifter_1_out, shifter_2_out,
       shifter_3_out, shifter_4_out, subtractor_1_out, subtractor_2_out, xor_1_out;

  assign and_1_out = A & B;  // AND_Gate and_1, 32 bits wide
  assign xor_1_out = A ^ B;  // XOR_Gate xor_1, 32 bits wide
  Shifter #(.width(32)) shifter_1 (.in(B), .\dist (Shift), .out(shifter_1_out));
  Shifter #(.shift("lr"), .width(32)) shifter_2 (.in(B), .\dist (Shift), .out(shifter_2_out));
  Shifter #(.shift("ar"), .width(32)) shifter_3 (.in(B), .\dist (Shift), .out(shifter_3_out));
  Adder #(.width(32)) adder_1 (.a(A), .b(B), .out(adder_1_out), .cin(CarryIn), .cout(OutAdd));
  not not_1 (not_1_out, CarryIn);
  Subtractor #(.width(32)) subtractor_1 (
    .a(B), .b(A), .out(subtractor_1_out), .bin(not_1_out), .bout(subtractor_1_bout));
  not not_2 (OutSub, subtractor_1_bout);
  Shifter #(.shift("rr"), .width(32)) shifter_4 (.in(B), .\dist (Shift), .out(shifter_4_out));
  assign AetB = A & B;  // AND_Gate and_2, 32 bits wide
  Subtractor #(.width(32)) subtractor_2 (.a({32{1'b0}}), .b(A), .out(subtractor_2_out));  // open: bin, bout
  Subtractor #(.width(32)) subtractor_3 (.a(B), .b(A), .out(BmoinsA), .bout(subtractor_3_bout));  // open: bin
  Adder #(.width(32)) adder_2 (.a(A), .b(B), .out(AplusB), .cout(CMN));  // open: cin
  assign or_1_out = A | B;  // OR_Gate or_1, 32 bits wide
  Multiplier #(.width(32)) multiplier_1 (.a(A), .b(B), .out(multiplier_1_out));  // open: cin, cout
  assign not_3_out = ~A;  // NOT_Gate not_3, 32 bits wide
  assign and_3_out = not_3_out & B;  // AND_Gate and_3, 32 bits wide
  assign not_4_out = ~A;  // NOT_Gate not_4, 32 bits wide
  not not_5 (CMP, subtractor_3_bout);
  Multiplexer #(.select(4), .width(32)) multiplexer_1 (
    .in0(and_1_out), .in1(xor_1_out), .in2(shifter_1_out), .in3(shifter_2_out), .in4(shifter_3_out),
    .in5(adder_1_out), .in6(subtractor_1_out), .in7(shifter_4_out), .in8(B), .in9(subtractor_2_out),
    .in10(B), .in11(B), .in12(or_1_out), .in13(multiplier_1_out), .in14(and_3_out), .in15(not_4_out),
    .out(S), .sel(Codop));
  assign not_6_out = ~A;  // NOT_Gate not_6, 32 bits wide
  Adder #(.width(32)) adder_3 (.a(not_6_out), .b(32'h1), .out(adder_3_out), .cout(adder_3_cout));  // open: cin
  Multiplexer #(.select(4)) multiplexer_2 (
    .in0(in_1), .in1(in_1), .in2(LSL), .in3(ASR), .in4(ASR), .in5(OutAdd), .in6(OutSub), .in7(ASR),
    .in8(in_1), .in9(adder_3_cout), .in10(CMP), .in11(CMN), .in12(in_1), .in13(in_1), .in14(in_1),
    .in15(in_1), .out(Flags[1]), .sel(Codop));
  Multiplexer #(.select(4), .width(32)) multiplexer_3 (
    .in0(S), .in1(S), .in2(S), .in3(S), .in4(S), .in5(S), .in6(S), .in7(S), .in8(AetB), .in9(S),
    .in10(BmoinsA), .in11(AplusB), .in12(S), .in13(S), .in14(S), .in15(S), .out(multiplexer_3_out),
    .sel(Codop));
  Subtractor #(.width(5)) subtractor_4 (.a(Shift), .b(5'b00001), .out(subtractor_4_out));  // open: bin, bout
  BitSelector #(.width(32)) bitselector_1 (.in(B), .out(ASR), .sel(subtractor_4_out));
  BitSelector #(.width(32)) bitselector_2 (.in(B), .out(LSL), .sel(subtractor_5_out));
  Subtractor #(.width(5)) subtractor_5 (.a({5{1'b0}}), .b(Shift), .out(subtractor_5_out));  // open: bin, bout
  Comparator #(.width(32)) comparator_1 (
    .a(multiplexer_3_out), .b({32{1'b0}}), .eq(Flags[2]), .lt(Flags[3]));  // open: gt
  Multiplexer #(.select(4)) multiplexer_4 (
    .in0(in_2), .in1(in_2), .in2(in_2), .in3(in_2), .in4(in_2), .in5(ResV), .in6(ResVsub), .in7(in_2),
    .in8(in_2), .in9(ResVAplusB), .in10(ResV), .in11(ResVAplusB), .in12(in_2), .in13(in_2), .in14(in_2),
    .in15(in_2), .out(Flags[0]), .sel(Codop));
  xnor xnor_1 (xnor_1_out, A[31], B[31]);
  xor xor_2 (xor_2_out, S[31], B[31]);
  xor xor_3 (xor_3_out, A[31], B[31]);
  xor xor_4 (xor_4_out, S[31], B[31]);
  xnor xnor_2 (xnor_2_out, A[31], B[31]);
  xor xor_5 (xor_5_out, AplusB[31], B[31]);
  and and_4 (ResV, xnor_1_out, xor_2_out);
  and and_5 (ResVsub, xor_3_out, xor_4_out);
  and and_6 (ResVAplusB, xnor_2_out, xor_5_out);

  // Other names for the same wires on the sheet: Overflow = Flags[0]; Carry = Flags[1]; Zero = Flags[2];
  //   Negative = Flags[3]; Res[31:0] = S; LSR = ASR; ROT = ASR; S_t[4:0] = Shift

  // Notes on the sheet:
  //   "0"
  //   Note: for ROR, C = N
  //   Note 2: assume that shift > 0 for LSL and LSR
  //   Gestion des Carry
  //   Negative
  //   Zero :
  //   Synthese des flags
  //   Xnor à faire entre les entrées A et B (dernier bit de chaque) et la sortie ( dernier bit) ( Si A et B sont positifs, alors le résultat doit etre positif)  
endmodule
