// Logisim project Ctl_Conditional.circ as structural Verilog: 1 circuit, main circuit Conditional
module Conditional (
  input  Enable,
  input  [15:0] Instruction,
  input  Z,
  input  C,
  input  N,
  input  V,
  output [10:0] Offset,
  output Verified
);

  wire and_1_out, and_2_out, and_3_out, and_5_out, Ci, Ci2, eight, eleven, five, four, Ni, nine, not_1_out,
       not_2_out, not_3_out, not_4_out, not_5_out, not_6_out, not_7_out, one, or_2_out, or_3_out, res8, res9,
       res10, res11, res12, res13, ResNotCond, seven, six, ten, thirteen, three, twelve, two, Verified_t, Vi,
       xnor_10_out, xnor_11_out, xnor_12_out, xnor_13_out, xnor_15_out, xnor_16_out, xnor_17_out, zero, Zi,
       Zi2;
  wire [10:0] bit_extender_1_out, bit_extender_2_out;

  // Probe on Z
  Multiplexer #(.select(4)) multiplexer_1 (
    .in0(1'b0), .in1(1'b0), .in2(1'b1), .in3(1'b0), .in4(1'b0), .in5(1'b0), .in6(1'b0), .in7(1'b0),
    .in8(1'b0), .in9(1'b0), .in10(1'b0), .in11(1'b0), .in12(1'b0), .in13(1'b0), .in14(1'b0), .in15(1'b0),
    .out(Ci), .sel(Instruction[11:8]));
  xnor xnor_1 (one, 1'b0, Z);
  // Probe on one
  Multiplexer #(.select(4)) multiplexer_2 (
    .in0(1'b0), .in1(1'b0), .in2(1'b0), .in3(1'b0), .in4(1'b0), .in5(1'b0), .in6(1'b0), .in7(1'b0),
    .in8(1'b0), .in9(1'b0), .in10(1'b0), .in11(1'b0), .in12(1'b0), .in13(1'b0), .in14(1'b0), .in15(1'b0),
    .out(Ci2), .sel(Instruction[11:8]));
  xnor xnor_2 (three, 1'b0, C);
  // Probe on three
  // Probe on Instruction[11:8]
  // Probe on Instruction[11:8]
  Multiplexer #(.select(4)) multiplexer_3 (
    .in0(1'b1), .in1(1'b0), .in2(1'b0), .in3(1'b0), .in4(1'b0), .in5(1'b0), .in6(1'b0), .in7(1'b0),
    .in8(1'b0), .in9(1'b0), .in10(1'b0), .in11(1'b0), .in12(1'b0), .in13(1'b0), .in14(1'b0), .in15(1'b0),
    .out(Zi), .sel(Instruction[11:8]));
  // Probe on Z
  Multiplexer #(.select(4)) multiplexer_4 (
    .in0(1'b0), .in1(1'b0), .in2(1'b0), .in3(1'b0), .in4(1'b0), .in5(1'b0), .in6(1'b0), .in7(1'b0),
    .in8(1'b0), .in9(1'b0), .in10(1'b0), .in11(1'b0), .in12(1'b0), .in13(1'b0), .in14(1'b0), .in15(1'b0),
    .out(Zi2), .sel(Instruction[11:8]));
  xnor xnor_3 (two, 1'b1, C);
  // Probe on two
  xnor xnor_4 (zero, 1'b1, Z);
  // Probe on zero
  xnor xnor_5 (five, 1'b0, N);
  // Probe on five
  Comparator #(.width(5)) comparator_1 (.a(Instruction[15:11]), .b(5'b11100), .eq(ResNotCond));  // open: gt, lt
  xnor xnor_6 (four, Ni, N);
  // Probe on V
  assign bit_extender_1_out = {{10{1'b0}}, 1'b0};  // Bit_Extender bit_extender_1
  assign bit_extender_2_out = {{3{Instruction[7]}}, Instruction[7:0]};  // Bit_Extender bit_extender_2
  Multiplexer #(.select(4)) multiplexer_5 (
    .in0(1'b0), .in1(1'b0), .in2(1'b0), .in3(1'b0), .in4(1'b1), .in5(1'b0), .in6(1'b0), .in7(1'b0),
    .in8(1'b0), .in9(1'b0), .in10(1'b0), .in11(1'b0), .in12(1'b0), .in13(1'b0), .in14(1'b0), .in15(1'b0),
    .out(Ni), .sel(Instruction[11:8]));
  // Probe on four
  // Probe on four
  xnor xnor_7 (seven, 1'b0, V);
  // Probe on seven
  Multiplexer #(.width(11)) multiplexer_6 (
    .in0(bit_extender_1_out), .in1(bit_extender_2_out), .out(Offset), .sel(Enable));
  and and_1 (and_1_out, Enable, Verified_t);
  and and_2 (and_2_out, ResNotCond, Enable);
  xnor xnor_8 (six, Vi, V);
  Multiplexer #(.select(4)) multiplexer_7 (
    .in0(zero), .in1(one), .in2(two), .in3(three), .in4(four), .in5(five), .in6(six), .in7(seven),
    .in8(eight), .in9(nine), .in10(ten), .in11(eleven), .in12(twelve), .in13(thirteen), .in14(1'b1),
    .out(Verified_t), .sel(Instruction[11:8]));  // open: in15
  // Probe on Verified_t
  or or_1 (Verified, and_1_out, and_2_out);
  Multiplexer #(.select(4)) multiplexer_8 (
    .in0(1'b0), .in1(1'b0), .in2(1'b0), .in3(1'b0), .in4(1'b0), .in5(1'b0), .in6(1'b1), .in7(1'b0),
    .in8(1'b0), .in9(1'b0), .in10(1'b0), .in11(1'b0), .in12(1'b0), .in13(1'b0), .in14(1'b0), .in15(1'b0),
    .out(Vi), .sel(Instruction[11:8]));
  // Probe on Instruction[11:8]
  not not_1 (not_1_out, Ci);
  or or_2 (or_2_out, not_1_out, Zi);
  not not_2 (not_2_out, C);
  Multiplexer #(.select(4)) multiplexer_9 (
    .in0(1'b0), .in1(1'b0), .in2(1'b0), .in3(1'b0), .in4(1'b0), .in5(1'b0), .in6(1'b0), .in7(1'b0),
    .in8(1'b0), .in9(or_2_out), .in10(1'b0), .in11(1'b0), .in12(1'b0), .in13(1'b0), .in14(1'b0), .in15(1'b0),
    .out(res9), .sel(Instruction[11:8]));
  or or_3 (or_3_out, not_2_out, Z);
  xnor xnor_9 (nine, res9, or_3_out);
  // Probe on nine
  // Probe on nine
  and and_3 (and_3_out, Ci, not_3_out);
  not not_3 (not_3_out, Zi);
  Multiplexer #(.select(4)) multiplexer_10 (
    .in0(1'b0), .in1(1'b0), .in2(1'b0), .in3(1'b0), .in4(1'b0), .in5(1'b0), .in6(1'b0), .in7(1'b0),
    .in8(and_3_out), .in9(1'b0), .in10(1'b0), .in11(1'b0), .in12(1'b0), .in13(1'b0), .in14(1'b0),
    .in15(1'b0), .out(res8), .sel(Instruction[11:8]));
  // Probe on nothing
  xnor xnor_10 (xnor_10_out, C, 1'b1);
  xnor xnor_11 (xnor_11_out, Z, 1'b0);
  xnor xnor_12 (xnor_12_out, Ni, Vi);
  xnor xnor_13 (xnor_13_out, N, V);
  and and_4 (eight, xnor_10_out, xnor_11_out);
  Multiplexer #(.select(4)) multiplexer_11 (
    .in0(1'b0), .in1(1'b0), .in2(1'b0), .in3(1'b0), .in4(1'b0), .in5(1'b0), .in6(1'b0), .in7(1'b0),
    .in8(1'b0), .in9(1'b0), .in10(xnor_12_out), .in11(1'b0), .in12(1'b0), .in13(1'b0), .in14(1'b0),
    .in15(1'b0), .out(res10), .sel(Instruction[11:8]));
  xnor xnor_14 (ten, res10, xnor_13_out);
  // Probe on ten
  // Probe on ten
  xnor xnor_15 (xnor_15_out, N, V);
  not not_4 (not_4_out, xnor_15_out);
  Multiplexer #(.select(4)) multiplexer_12 (
    .in0(1'b0), .in1(1'b0), .in2(1'b0), .in3(1'b0), .in4(1'b0), .in5(1'b0), .in6(1'b0), .in7(1'b0),
    .in8(1'b0), .in9(1'b0), .in10(1'b0), .in11(not_4_out), .in12(1'b0), .in13(1'b0), .in14(1'b0),
    .in15(1'b0), .out(res11), .sel(Instruction[11:8]));
  xor xor_1 (eleven, N, V);
  not not_5 (not_5_out, Z);
  and and_5 (and_5_out, not_5_out, res11);
  // Probe on eleven
  // Probe on eleven
  Multiplexer #(.select(4)) multiplexer_13 (
    .in0(1'b0), .in1(1'b0), .in2(1'b0), .in3(1'b0), .in4(1'b0), .in5(1'b0), .in6(1'b0), .in7(1'b0),
    .in8(1'b0), .in9(1'b0), .in10(1'b0), .in11(1'b0), .in12(and_5_out), .in13(1'b0), .in14(1'b0),
    .in15(1'b0), .out(res12), .sel(Instruction[11:8]));
  not not_6 (not_6_out, res12);
  xnor xnor_16 (xnor_16_out, Z, 1'b0);
  not not_7 (not_7_out, eleven);
  and and_6 (twelve, xnor_16_out, not_7_out);
  // Probe on twelve
  // Probe on twelve
  Multiplexer #(.select(4)) multiplexer_14 (
    .in0(1'b0), .in1(1'b0), .in2(1'b0), .in3(1'b0), .in4(1'b0), .in5(1'b0), .in6(1'b0), .in7(1'b0),
    .in8(1'b0), .in9(1'b0), .in10(1'b0), .in11(1'b0), .in12(1'b0), .in13(not_6_out), .in14(1'b0),
    .in15(1'b0), .out(res13), .sel(Instruction[11:8]));
  or or_4 (thirteen, eleven, xnor_17_out);
  xnor xnor_17 (xnor_17_out, Z, 1'b1);
  // Probe on thirteen

  // Other names for the same wires on the sheet: Offset_t[7:0] = Instruction[7:0]; Inst[3:0] = Instruction[11:8];
  //   NotCond[4:0] = Instruction[15:11]
endmodule
