// Logisim project Ctl_Data_Processing.circ as structural Verilog: 1 circuit, main circuit Data_Processing
module Data_Processing (
  input  Enable,
  input  [15:0] Instruction,
  output [2:0] Rd,
  output [2:0] Rn,
  output [2:0] Rm,
  output [3:0] ALU_Opcode,
  output [3:0] Flags_Update_Mask
);

  wire [2:0] Res012, Res345;
  wire [3:0] multiplexer_4_out;
  wire [15:0] Instruction_t;

  BitSelector #(.group(3), .width(16)) bitselector_1 (
    .in({Instruction_t[15:10], ALU_Opcode, Instruction_t[5:0]}), .out(Res012), .sel(3'b000));
  BitSelector #(.group(3), .width(16)) bitselector_2 (
    .in({Instruction_t[15:10], ALU_Opcode, Instruction_t[5:0]}), .out(Res345), .sel(3'b001));
  Multiplexer #(.select(4), .width(3)) multiplexer_1 (
    .in0(Res012), .in1(Res012), .in2(Res012), .in3(Res012), .in4(Res012), .in5(Res012), .in6(Res012),
    .in7(Res012), .in8(Res012), .in9(Res345), .in10(Res012), .in11(Res012), .in12(Res012), .in13(Res345),
    .in14(Res012), .in15(Res012), .out(Rn), .sel(ALU_Opcode));
  Multiplexer #(.width(16)) multiplexer_2 (
    .in0({16{1'b0}}), .in1(Instruction), .out({Instruction_t[15:10], ALU_Opcode, Instruction_t[5:0]}),
    .sel(Enable));
  Multiplexer #(.select(4), .width(3)) multiplexer_3 (
    .in0(Res345), .in1(Res345), .in2(Res345), .in3(Res345), .in4(Res345), .in5(Res345), .in6(Res345),
    .in7(Res345), .in8(Res345), .in9(Res345), .in10(Res345), .in11(Res345), .in12(Res345), .in13(Res012),
    .in14(Res345), .in15(Res345), .out(Rm), .sel(ALU_Opcode));
  Multiplexer #(.select(4), .width(4)) multiplexer_4 (
    .in0(4'b1110), .in1(4'b1110), .in2(4'b1110), .in3(4'b1110), .in4(4'b1110), .in5(4'b1111), .in6(4'b1111),
    .in7(4'b1110), .in8(4'b1110), .in9(4'b1111), .in10(4'b1111), .in11(4'b1111), .in12(4'b1110),
    .in13(4'b1100), .in14(4'b1110), .in15(4'b1110), .out(multiplexer_4_out), .sel(ALU_Opcode));
  Multiplexer #(.width(4)) multiplexer_5 (
    .in0(4'b0000), .in1(multiplexer_4_out), .out(Flags_Update_Mask), .sel(Enable));
  Multiplexer #(.select(4), .width(3)) multiplexer_6 (
    .in0(Rn), .in1(Rn), .in2(Rn), .in3(Rn), .in4(Rn), .in5(Rn), .in6(Rn), .in7(Rn), .in8(Rn), .in9(Res012),
    .in10(Rn), .in11(Rn), .in12(Rn), .in13(Rm), .in14(Rn), .in15(Rn), .out(Rd), .sel(ALU_Opcode));

  // Other names for the same wires on the sheet: Flags[3:0] = Flags_Update_Mask; Instruction_t[9:6] = ALU_Opcode;
  //   Opcode[3:0] = ALU_Opcode

  // Notes on the sheet:
  //   Choix de l'instruction
  //   Note 2: RSB instruction has Rn as 1st operand.
  //   MUL instruction has Rn as 1st operand and Rdm as 2nd operand
  //   For simplification purposes, Rm is used for 1st operand both here and in the ALU.
  //   Note: instructions that does not save the result will still have the second operand as the destination register, the ALU will copy the second register to the destination register
  //   Pull output low on Enable = 0
  //   Operandes A et B pour operation entre le contenu du registre Rdn et le contenu du registre Rm
endmodule
