// Logisim project Ctl_Flags_APSR.circ as structural Verilog: 1 circuit, main circuit Flags_APSR
module Flags_APSR (
  input  Clk,
  input  [3:0] Update_Mask,
  input  Rst,
  input  [3:0] Flags_In,
  input  in_5,
  input  in_6,
  input  in_7,
  output [3:0] Flags_Out
);

  Register #(.width(1)) register_1 (.D(Flags_In[0]), .en(Update_Mask[0]), .clk(Clk), .Q(Flags_Out[0]), .clr(Rst));
  Register #(.width(1)) register_2 (.D(Flags_In[1]), .en(Update_Mask[1]), .clk(Clk), .Q(Flags_Out[1]), .clr(in_5));
  Register #(.width(1)) register_3 (.D(Flags_In[2]), .en(Update_Mask[2]), .clk(Clk), .Q(Flags_Out[2]), .clr(in_6));
  Register #(.width(1)) register_4 (.D(Flags_In[3]), .en(Update_Mask[3]), .clk(Clk), .Q(Flags_Out[3]), .clr(in_7));

  // Other names for the same wires on the sheet: F0 = Flags_In[0]; F1 = Flags_In[1]; F2 = Flags_In[2];
  //   F3 = Flags_In[3]; UM0 = Update_Mask[0]; UM1 = Update_Mask[1]; UM2 = Update_Mask[2]; UM3 = Update_Mask[3]
endmodule
