// Logisim project Ctl_Load_Store.circ as structural Verilog: 1 circuit, main circuit Load_Store
module Load_Store (
  input  [15:0] Instruction,
  input  Enable,
  input  [31:0] Stack_Pointer,
  input  Clk,
  input  Reset,
  output Store,
  output [2:0] Rmd,
  output [31:0] RAM_Addr,
  output Load,
  output PC_Hold
);

  wire and_1_out, d_ff_1_q, d_ff_1_qn, not_1_out, not_2_out, not_3_out, or_1_out;
  wire [2:0] bit_extender_2_out;
  wire [31:0] add, bit_extender_1_out, bit_extender_3_out;

  not not_1 (not_1_out, d_ff_1_q);
  assign bit_extender_1_out = {{24{Instruction[7]}}, Instruction[7:0]};  // Bit_Extender bit_extender_1
  D_Flip_Flop d_ff_1 (.D(and_1_out), .clk(not_2_out), .Q(d_ff_1_q), .Qn(d_ff_1_qn), .reset(or_1_out));  // open: preset
  and and_1 (and_1_out, not_1_out, Instruction[11]);
  not not_2 (not_2_out, Clk);
  or or_1 (or_1_out, ~Instruction[11], Reset, ~Enable);  // OR_Gate
  Adder #(.width(32)) adder_1 (.a(bit_extender_1_out), .b(Stack_Pointer), .out(add));  // open: cin, cout
  and and_2 (Load, Enable, Instruction[11], d_ff_1_q);
  and and_3 (PC_Hold, d_ff_1_qn, Enable, Instruction[11]);
  assign bit_extender_2_out = {{2{Enable}}, Enable};  // Bit_Extender bit_extender_2
  assign bit_extender_3_out = {{31{Enable}}, Enable};  // Bit_Extender bit_extender_3
  assign Rmd = bit_extender_2_out & Instruction[10:8];  // AND_Gate and_4, 3 bits wide
  assign RAM_Addr = bit_extender_3_out & add;  // AND_Gate and_5, 32 bits wide
  not not_3 (not_3_out, Instruction[11]);
  and and_6 (Store, Enable, not_3_out);

  // Other names for the same wires on the sheet: imm8[7:0] = Instruction[7:0]; Rt[2:0] = Instruction[10:8];
  //   opcod = Instruction[11]

  // Notes on the sheet:
  //   Instruction: pull=down
  //   Delay load and hold PC for 1 cycle for the RAM to send out requested data 
endmodule
