// Logisim project Ctl_Shift_Add_Sub_Mov.circ as structural Verilog
module Shift_Add_Sub_Mov (
  input  Enable,
  input  [15:0] Instruction,
  output [3:0] Flags_Update_Mask,
  output Carry,
  output Imm32_Enable,
  output [2:0] Rm,
  output [2:0] Rn,
  output [2:0] Rd,
  output [4:0] Imm5,
  output [31:0] Imm32,
  output [3:0] ALU_Opcode
);

  wire add_i, add_r, and_2_out, and_3_out, and_5_out, and_6_out, and_9_out, and_10_out, and_12_out, i_AD,
       i_ADD, i_ASR, i_CMP, i_LSL, i_LSR, i_MOV, i_SUB, not_1_out, not_2_out, not_3_out, not_4_out,
       not_5_out, or_2_out, or_3_out, or_5_out, or_6_out, or_7_out, or_10_out, or_11_out, select_Rm, sub_i,
       sub_r;
  wire [2:0] imm3, multiplexer_1_out, multiplexer_6_out, Rd_t, Rm_t, Rn_t;
  wire [3:0] bit_extender_3_out, bit_extender_4_out, flags_to_update_1_flags_update_mask, opcode_alu_1_sortie;
  wire [7:0] imm8;
  wire [15:0] and_4_out, and_11_out, and_13_out, and_14_out, and_15_out, bit_extender_1_out,
       bit_extender_2_out, bit_extender_5_out, bit_extender_7_out, bit_extender_9_out, bit_extender_10_out,
       INST;
  wire [31:0] bit_extender_6_out, bit_extender_8_out, multiplexer_9_out, negator_1_out;

  assign bit_extender_1_out = {{15{Enable}}, Enable};  // Bit_Extender bit_extender_1
  Multiplexer #(.width(3)) multiplexer_1 (
    .in0(Instruction[8:6]), .in1(3'b000), .out(multiplexer_1_out), .sel(Instruction[10]));
  assign INST = Instruction & bit_extender_1_out;  // AND_Gate and_1, 16 bits wide
  not not_1 (not_1_out, Instruction[11]);
  and and_2 (and_2_out, not_1_out, not_2_out);
  not not_2 (not_2_out, Instruction[13]);
  not not_3 (not_3_out, Instruction[13]);
  and and_3 (and_3_out, not_3_out, not_4_out);
  not not_4 (not_4_out, Instruction[12]);
  Multiplexer #(.width(3)) multiplexer_2 (.in0(multiplexer_1_out), .in1(Instruction[5:3]), .out(Rm_t), .sel(select_Rm));
  or or_1 (select_Rm, and_2_out, and_3_out);
  assign bit_extender_2_out = {{15{Enable}}, Enable};  // Bit_Extender bit_extender_2
  Multiplexer #(.width(3)) multiplexer_3 (.in0(3'b000), .in1(Rm_t), .out(Rm), .sel(Enable));
  Multiplexer #(.width(3)) multiplexer_4 (.in0(3'b000), .in1(Rn_t), .out(Rn), .sel(Enable));
  Multiplexer #(.width(3)) multiplexer_5 (.in0(3'b000), .in1(Rd_t), .out(Rd), .sel(Enable));
  assign and_4_out = Instruction & bit_extender_2_out;  // AND_Gate and_4, 16 bits wide
  Multiplexer #(.width(3)) multiplexer_6 (
    .in0(3'b000), .in1(Instruction[10:8]), .out(multiplexer_6_out), .sel(and_5_out));
  and and_5 (and_5_out, Instruction[13], Instruction[12]);
  not not_5 (not_5_out, Instruction[13]);
  and and_6 (and_6_out, Instruction[11], Instruction[12], not_5_out);
  assign bit_extender_3_out = {{3{Enable}}, Enable};  // Bit_Extender bit_extender_3
  Multiplexer #(.width(3)) multiplexer_7 (.in0(multiplexer_6_out), .in1(Instruction[5:3]), .out(Rn_t), .sel(or_2_out));
  or or_2 (or_2_out, select_Rm, and_6_out);
  Flags_To_Update flags_to_update_1 (.codop(and_4_out[13:11]), .flags_update_mask(flags_to_update_1_flags_update_mask));
  assign bit_extender_4_out = {{3{Enable}}, Enable};  // Bit_Extender bit_extender_4
  or or_3 (or_3_out, sub_i, sub_r);
  assign ALU_Opcode = bit_extender_3_out & opcode_alu_1_sortie;  // AND_Gate and_7, 4 bits wide
  opcode_ALU opcode_alu_1 (.Entree(Instruction[13:9]), .Sortie(opcode_alu_1_sortie));
  assign Flags_Update_Mask = bit_extender_4_out & flags_to_update_1_flags_update_mask;  // AND_Gate and_8, 4 bits wide
  Decoder #(.select(3)) decoder_1 (
    .out0(i_LSL), .out1(i_LSR), .out2(i_ASR), .out3(i_AD), .out4(i_MOV), .out5(i_CMP), .out6(i_ADD),
    .out7(i_SUB), .sel(INST[13:11]));  // open: en
  Decoder #(.select(2)) decoder_2 (
    .out0(add_r), .out1(sub_r), .out2(add_i), .out3(sub_i), .sel(INST[10:9]));  // open: en
  and and_9 (and_9_out, or_3_out, i_AD);
  Multiplexer #(.width(3)) multiplexer_8 (
    .in0(Instruction[2:0]), .in1(Instruction[10:8]), .out(Rd_t), .sel(Instruction[13]));
  or or_4 (Carry, and_9_out, i_SUB);
  or or_5 (or_5_out, i_LSL, i_LSR, i_ASR);
  and and_10 (and_10_out, i_AD, or_6_out);
  or or_6 (or_6_out, add_i, sub_i);
  or or_7 (or_7_out, add_i, sub_i);
  assign bit_extender_5_out = {{15{or_5_out}}, or_5_out};  // Bit_Extender bit_extender_5
  assign {and_11_out[15:11], Imm5, and_11_out[5:0]} = bit_extender_5_out & INST;  // AND_Gate and_11, 16 bits wide
  assign bit_extender_6_out = {{24{1'b0}}, imm8};  // Bit_Extender bit_extender_6
  assign bit_extender_7_out = {{15{and_12_out}}, and_12_out};  // Bit_Extender bit_extender_7
  and and_12 (and_12_out, i_AD, or_7_out);
  Negator #(.width(32)) negator_1 (.in(bit_extender_6_out), .out(negator_1_out));
  assign {and_13_out[15:9], imm3, and_13_out[5:0]} = bit_extender_7_out & INST;  // AND_Gate and_13, 16 bits wide
  or or_8 (Imm32_Enable, and_10_out, i_MOV, i_CMP, i_ADD, i_SUB);
  assign bit_extender_8_out = {{29{1'b0}}, imm3};  // Bit_Extender bit_extender_8
  Multiplexer #(.width(32)) multiplexer_9 (
    .in0(bit_extender_6_out), .in1(negator_1_out), .out(multiplexer_9_out), .sel(i_MOV));
  assign Imm32 = bit_extender_8_out | multiplexer_9_out;  // OR_Gate or_9, 32 bits wide
  or or_10 (or_10_out, i_MOV, i_CMP);
  or or_11 (or_11_out, i_ADD, i_SUB);
  // Probe on Imm32
  assign bit_extender_9_out = {{15{or_10_out}}, or_10_out};  // Bit_Extender bit_extender_9
  assign bit_extender_10_out = {{15{or_11_out}}, or_11_out};  // Bit_Extender bit_extender_10
  assign and_14_out = bit_extender_9_out & INST;  // AND_Gate and_14, 16 bits wide
  assign and_15_out = bit_extender_10_out & INST;  // AND_Gate and_15, 16 bits wide
  assign imm8 = and_14_out[7:0] | and_15_out[7:0];  // OR_Gate or_12, 8 bits wide

  // Other names for the same wires on the sheet: Bit0_2[2:0] = Instruction[2:0]; Bit0_7[7:0] = Instruction[7:0];
  //   Bit3_5[2:0] = Instruction[5:3]; Bit6_8[2:0] = Instruction[8:6]; Bit6_10[4:0] = Instruction[10:6];
  //   Bit8_10[2:0] = Instruction[10:8]; Index10 = Instruction[10]; Bit11_12op[1:0] = Instruction[12:11];
  //   Bit13_11op[2:0] = Instruction[13:11]; Index12 = Instruction[12]; Bit13_15[2:0] = Instruction[15:13];
  //   Index13 = Instruction[13]

  // Notes on the sheet:
  //   Note 3: Imm32_Enable forces the use of the immediate for Rm register
  //   Note: ALU uses Rn register for shifts. Use Rn instead of Rm for shifts (immediate) here too
  //   Note 2: MOV uses RSB ALU opcode with Imm8 reversed so that it is copied to output register
  //   Pull output low on Enable = 0
  //   only ADD and SUB use Rm
  //   Enable carry for SUB since it is reversed in ALU
  //   ALU will use Imm32 instead of Rm
endmodule

module opcode_ALU (
  input  [4:0] Entree,
  output [3:0] Sortie
);

  wire and_2_out, and_3_out, and_4_out, and_5_out, and_6_out, and_7_out, not_1_out, not_2_out, not_3_out,
       not_4_out;

  not not_1 (not_1_out, Entree[4]);
  not not_2 (not_2_out, Entree[3]);
  not not_3 (not_3_out, Entree[2]);
  not not_4 (not_4_out, Entree[0]);
  and and_1 (Sortie[3], Entree[4], not_2_out);
  and and_2 (and_2_out, not_1_out, not_2_out);
  and and_3 (and_3_out, Entree[2], Entree[0]);
  and and_4 (and_4_out, Entree[4], Entree[2]);
  and and_5 (and_5_out, not_1_out, not_2_out, Entree[2]);
  and and_6 (and_6_out, not_1_out, Entree[2], not_4_out);
  and and_7 (and_7_out, Entree[4], not_3_out);
  or or_1 (Sortie[1], and_2_out, and_3_out, and_4_out);
  or or_2 (Sortie[0], and_5_out, and_6_out, and_7_out);

  assign Sortie[2] = Entree[3];
endmodule

module Flags_To_Update (
  input  [2:0] codop,
  output [3:0] flags_update_mask
);

  wire and_1_out, and_2_out, and_3_out, not_1_out;

  not not_1 (not_1_out, codop[2]);
  or or_1 (flags_update_mask[1], not_1_out, codop[0], codop[1]);
  and and_1 (and_1_out, codop[1], codop[0]);
  and and_2 (and_2_out, codop[2], codop[0]);
  and and_3 (and_3_out, codop[2], codop[1]);
  or or_2 (flags_update_mask[0], and_1_out, and_2_out, and_3_out);

  assign flags_update_mask[3:2] = 2'b11;
endmodule
